// Logisim project dec to binary.circ as structural Verilog: 1 circuit, main circuit main
module main (
  input  _1,
  input  _2,
  input  _3,
  input  _4,
  input  _5,
  input  _6,
  input  _7,
  input  _8,
  input  _9,
  input  _10,
  input  _11,
  input  _12,
  input  _13,
  input  _14,
  input  _15,
  output out_16,
  output out_17,
  output out_18,
  output out_19
);

  or or_1 (out_19, _15, _13, _1, _3, _5, _7, _9, _11);
  or or_2 (out_18, _14, _11, _2, _7, _6, _10, _3, _15, _15);
  or or_3 (out_17, _13, _4, _5, _6, _7, _12, _14, _15);
  or or_4 (out_16, _13, _9, _10, _12, _8, _11, _14, _15);

  // Notes on the sheet:
  //   4-bit decimical-to-binary encoder
  //   This circuit is a 4-bit decimical-to-binary encoder designed using basic logic gates. It takes one active input among 16 lines. OR gates are used to generate each output bits.
endmodule
